# Fritzing sketch bewaesserungssystem_circuit_fritzing (saved by Fritzing 0.9.4)

parts:
  Arduino_Nano = Arduino Nano (Rev3.0)
  Q1 = NPN-Transistor [package="TO92 [THT]"]
  Q2 = NPN-Transistor [package="TO92 [THT]"]
  M1 = DC Motor
  M2 = DC Motor
  R1 = Resistor [tolerance=±5% resistance=470 package=THT]
  R2 = Resistor [tolerance=±5% resistance=470 package=THT]
  D1 = Rectifier Diode [part_number=1N4001 package="300 mil [THT]"]
  D2 = Rectifier Diode [part_number=1N4001 package="300 mil [THT]"]
  Capacitive_Soil_Moisture_Sensor1 = DFRobot Capacitive Soil Moisture Sensor V1.0 [part_number=SEN0193]
  Capacitive_Soil_Moisture_Sensor2 = DFRobot Capacitive Soil Moisture Sensor V1.0 [part_number=SEN0193]

nets:
  GND: Arduino_Nano.GND, Q1.E, Q2.E, Capacitive_Soil_Moisture_Sensor1.GND, Capacitive_Soil_Moisture_Sensor2.GND
  N1: Arduino_Nano.D5, R1.Pin_0
  N2: Arduino_Nano.D6, R2.Pin_0
  5V: Arduino_Nano.5V, M1.pin_1, M2.pin_1, D1.cathode, D2.cathode, Capacitive_Soil_Moisture_Sensor1.VCC, Capacitive_Soil_Moisture_Sensor2.VCC
  N3: Arduino_Nano.A2, Capacitive_Soil_Moisture_Sensor2.A
  N4: Arduino_Nano.A1, Capacitive_Soil_Moisture_Sensor1.A
  N5: Q1.B, R1.Pin_1
  N6: Q1.C, M2.pin_2, D1.anode
  N7: Q2.B, R2.Pin_1
  N8: Q2.C, M1.pin_2, D2.anode

custom parts:
  DFRobot Capacitive Soil Moisture Sensor V1.0: DFRobot Capacitive Soil Moisture Sensor V1.0 This product measures soil moisture levels by capacitive sensing, rather than resistive sensing like other types of moisture sensor. It is made of a corrosion resistant material giving it a long service life. Insert it into soil and impress your friends with the real-time soil moisture data! The product includes an on-board voltage regulator which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
